// Logisim project register.circ as structural Verilog: 1 circuit, main circuit main
module main (
  input  [7:0] in_1,
  output out_2
);

  wire and_1_out, button_1_out, clock_1_out, OUT1, OUT2, xor_1_out;
  wire [5:0] register_1_q;

  LED #(.active("true")) led_1 (.in(OUT1));
  LED #(.active("true")) led_2 (.in(OUT2));
  Register #(.width(8), .trigger("rising")) register_1 (
    .D(in_1), .en(1'b1), .Q({OUT2, OUT1, register_1_q}), .clk(clock_1_out), .clr(button_1_out));
  Clock #(.highDuration(1), .lowDuration(1)) clock_1 (.out(clock_1_out));
  Button button_1 (.out(button_1_out));
  // Probe on and_1_out
  and and_1 (and_1_out, register_1_q[1], register_1_q[0]);
  or or_1 (out_2, register_1_q[2], register_1_q[3]);
  LED #(.active("true")) led_3 (.in(xor_1_out));
  xor xor_1 (xor_1_out, register_1_q[5], register_1_q[4]);

  // Notes on the sheet:
  //   Jessie McGarry
endmodule
