// Logisim project xor.circ as structural Verilog: 1 circuit, main circuit main
module main (
  input  x,
  input  y,
  output out_3
);

  wire and_1_out, and_2_out, not_1_out, not_2_out;

  not not_1 (not_1_out, x);
  and and_1 (and_1_out, not_1_out, y);
  and and_2 (and_2_out, x, not_2_out);
  not not_2 (not_2_out, y);
  or or_1 (out_3, and_1_out, and_2_out);

  // Notes on the sheet:
  //    8/29/10
  //   XOR Circuit
  //   Jessie McGarry
endmodule
