// Logisim project FullAdder.circ as structural Verilog: 1 circuit, main circuit main
module main (
  input  Carry_In,
  input  in_2,
  input  in_3,
  output Answer,
  output Carry_Out
);

  wire and_1_out, and_2_out, or_1_out, xor_1_out;

  xor xor_1 (xor_1_out, in_2, in_3);
  or or_1 (or_1_out, in_2, in_3);
  xor xor_2 (Answer, Carry_In, xor_1_out);
  and and_1 (and_1_out, Carry_In, or_1_out);
  and and_2 (and_2_out, in_2, in_3);
  or or_2 (Carry_Out, and_1_out, and_2_out);
endmodule
