// Logisim project HW3problem2.circ as structural Verilog: 1 circuit, main circuit main
module main (
  input  S0,
  input  S1,
  input  S2,
  input  A,
  input  B,
  input  Carry_In,
  output Answer,
  output Carry_Out
);

  wire and_1_out, and_2_out, and_3_out, and_4_out, and_5_out, nor_1_out, nor_2_out, nor_3_out, not_1_out,
       or_1_out, xor_1_out, xor_2_out;

  not not_1 (not_1_out, S0);
  nor nor_1 (nor_1_out, S1, S2);
  and and_1 (and_1_out, not_1_out, S1, S2);
  nor nor_2 (nor_2_out, S0, S2);
  and and_2 (and_2_out, nor_2_out, S1);
  nor nor_3 (nor_3_out, S0, S1);
  and and_3 (and_3_out, nor_3_out, S2);
  and and_4 (and_4_out, S0, nor_1_out);
  xor xor_1 (xor_1_out, and_3_out, B);
  or or_1 (or_1_out, and_3_out, and_2_out, Carry_In);
  and and_5 (and_5_out, and_2_out, B);
  xor xor_2 (xor_2_out, and_5_out, xor_1_out);
  FullAdder_main main_1 (.Carry_In(A), .in_2(xor_2_out), .in_3(or_1_out), .Answer(Answer), .Carry_Out(Carry_Out));

  // Notes on the sheet:
  //   And
  //   Increment
  //   Subtraction
  //   Or
  //   000 = Addition, 001 = Subtraction, 010 = Increment
  //   (from top to bottom)
endmodule
