// Logisim project stackcalc.circ as structural Verilog: 2 circuits, main circuit main
module main (
  input  in_1,
  input  [3:0] in_2,
  output [3:0] out_3,
  output [3:0] out_4
);

  wire ADD_out, cADD1, cADD2, cADD3, cDUMMY, cIDLE, CLK, CLK_out, cPOP, cPUSH1, cPUSH2, or_1_out, or_2_out,
       or_3_out, POP_out, PUSH_out, RESET, Step_out;
  wire [3:0] adder_1_out, multiplexer_2_out, RegA_q, RegB_q;

  Button Step (.out(Step_out));
  Clock #(.highDuration(1), .lowDuration(1)) u_CLK (.out(CLK_out));
  Button u_RESET (.out(RESET));
  Multiplexer #(.select(1), .width(1)) multiplexer_1 (.in0(Step_out), .in1(CLK_out), .out(CLK), .sel(in_1));
  or or_1 (or_1_out, cPOP, cPUSH1, cADD1);
  Button PUSH (.out(PUSH_out));
  Button POP (.out(POP_out));
  Button ADD (.out(ADD_out));
  or or_2 (or_2_out, cADD1, cPOP);
  Counter #(.width(4), .max('hf), .ongoal("wrap"), .trigger("rising")) counter_1 (
    .load(or_2_out), .D(out_4), .count(or_1_out), .Q(out_4), .clk(CLK), .clr(RESET));  // open: carry
  Multiplexer #(.select(1), .width(4)) multiplexer_2 (
    .in0(in_2), .in1(adder_1_out), .out(multiplexer_2_out), .sel(cADD3));
  statemachine statemachine_1 (
    .in_3(PUSH_out), .in_4(POP_out), .in_5(ADD_out), .in_1(CLK), .in_2(RESET), .out_6(cIDLE), .out_7(cDUMMY),
    .out_8(cPUSH1), .out_9(cPUSH2), .out_10(cPOP), .out_11(cADD1), .out_12(cADD2), .out_13(cADD3));
  or or_3 (or_3_out, cADD3, cPUSH2);
  RAM #(.addrWidth(4), .dataWidth(4), .bus("separate")) ram_1 (
    .addr(out_4), .din(multiplexer_2_out), .data(out_3), .str(or_3_out), .clk(CLK), .clr(RESET));  // open: sel, ld
  Register #(.width(4), .trigger("rising")) RegA (.D(out_3), .en(cADD1), .Q(RegA_q), .clk(CLK), .clr(RESET));
  Register #(.width(4), .trigger("rising")) RegB (.D(out_3), .en(cADD2), .Q(RegB_q), .clk(CLK), .clr(RESET));
  Adder #(.width(4)) adder_1 (.a(RegA_q), .b(RegB_q), .out(adder_1_out));  // open: cin, cout
endmodule

module statemachine (
  input  in_1,
  input  in_2,
  input  in_3,
  input  in_4,
  input  in_5,
  output out_6,
  output out_7,
  output out_8,
  output out_9,
  output out_10,
  output out_11,
  output out_12,
  output out_13
);

  wire and_1_out, and_2_out, and_6_out, nADD1, nDUMMY, nIDLE, nor_1_out, not_1_out, not_2_out, not_3_out,
       not_4_out, not_5_out, not_6_out, nPOP, nPUSH1, or_2_out, or_3_out;

  not not_1 (not_1_out, in_3);
  not not_2 (not_2_out, in_4);
  not not_3 (not_3_out, in_5);
  not not_4 (not_4_out, nPUSH1);
  not not_5 (not_5_out, nPOP);
  not not_6 (not_6_out, nADD1);
  and and_1 (and_1_out, out_7, not_1_out, not_2_out, not_3_out);
  nor nor_1 (nor_1_out, out_6, out_7, out_8, out_9, out_10, out_11, out_12, out_13);
  and and_2 (and_2_out, not_4_out, not_5_out, not_6_out, out_6);
  Register #(.width(8), .trigger("rising")) register_1 (
    .D({out_12, out_11, nADD1, nPOP, out_8, nPUSH1, nDUMMY, nIDLE}),
    .Q({out_13, out_12, out_11, out_10, out_9, out_8, out_7, out_6}), .clk(in_1), .clr(in_2));  // open: en
  and and_3 (nPUSH1, in_3, out_6);
  and and_4 (nPOP, in_4, out_6);
  and and_5 (nADD1, in_5, out_6);
  or or_1 (nIDLE, and_1_out, nor_1_out, and_2_out);
  or or_2 (or_2_out, out_9, out_10, out_13);
  or or_3 (or_3_out, in_3, in_4, in_5);
  and and_6 (and_6_out, out_7, or_3_out);
  or or_4 (nDUMMY, or_2_out, and_6_out);

  // Other names for the same wires on the sheet: ADDB = in_5; POPB = in_4; PUSHB = in_3; cIDLE = out_6;
  //   STATE[7:0] = {out_13, out_12, out_11, out_10, out_9, out_8, out_7, out_6}; cDUMMY = out_7; cPUSH1 = out_8;
  //   nPUSH2 = out_8; cPUSH2 = out_9; cPOP = out_10; cADD1 = out_11; nADD2 = out_11; cADD2 = out_12; nADD3 = out_12;
  //   cADD3 = out_13
endmodule
