// Logisim project lab4Part1.circ as structural Verilog: 1 circuit, main circuit main
module main (
  input  A,
  input  B,
  output out_3
);

  wire transistor_1_p3, transistor_7_p3;

  // Transistor #(.Type("N-Type"), .Power_Location("Top/Left")) transistor_1: pin names not known; wires that end beside it: A, 1'b1, transistor_1_p3
  Transistor #(.Type("N-Type"), .Power_Location("Top/Left")) transistor_2 (.out(B));  // open: in, gate
  Transistor #(.Type("N-Type"), .Power_Location("Top/Left")) transistor_3 (.out(A));  // open: in, gate
  Transistor #(.Type("P-Type"), .Power_Location("Top/Left")) transistor_4 (.out(B));  // open: in, gate
  Transistor #(.Type("P-Type"), .Power_Location("Top/Left")) transistor_5 (.in(A), .out(A));  // open: gate
  Transistor #(.Type("N-Type"), .Power_Location("Top/Left")) transistor_6 (.out(B));  // open: in, gate
  // Transistor #(.Type("P-Type"), .Power_Location("Bottom/Right")) transistor_7: pin names not known; wires that end beside it: A, out_3, transistor_7_p3
  // Transistor #(.Type("P-Type"), .Power_Location("Bottom/Right")) transistor_8: pin names not known; wires that end beside it: B, transistor_7_p3, transistor_7_p3, 1'b0
endmodule
