// Logisim project lab4Part2.circ as structural Verilog: 1 circuit, main circuit main
module main (
  input  in_1,
  input  in_2,
  input  in_3,
  input  in_4,
  input  in_5,
  input  in_6,
  input  in_7,
  input  in_8,
  input  in_9,
  input  in_10,
  output out_11,
  output out_12,
  output out_13,
  output out_14,
  output out_15,
  output out_16,
  output out_17
);

  wire and_5_out, and_6_out, and_7_out, and_8_out, not_1_out, not_2_out, not_3_out;

  not not_1 (not_1_out, in_1);
  not not_2 (not_2_out, in_3);
  and and_1 (out_11, not_1_out, not_2_out);
  and and_2 (out_13, in_1, not_2_out);
  and and_3 (out_14, in_3, not_1_out);
  and and_4 (out_16, in_3, in_1);
  and and_5 (and_5_out, out_11, in_7);
  and and_6 (and_6_out, out_13, in_8);
  and and_7 (and_7_out, out_14, in_9);
  and and_8 (and_8_out, out_16, in_10);
  ExactlyOne xor_1 (.out(out_17), .in0(and_5_out), .in1(and_6_out), .in2(and_7_out), .in3(and_8_out));
  not not_3 (not_3_out, in_4);
  and and_9 (out_12, in_2, not_3_out);
  or or_1 (out_15, in_5, in_6);

  // Other names for the same wires on the sheet: Dec1 = out_11; Dec2 = out_13; Dec3 = out_14; Dec4 = out_16

  // Notes on the sheet:
  //   Decoder
  //   Multiplexer
  //   Encoder
endmodule
