// Logisim project lab4part3.circ as structural Verilog: 1 circuit, main circuit main
module main (
);

  wire cAll, cBlue, cGreen, clock_1_out, cNone, cRed, nNone, nor_1_out, or_2_out, or_3_out, or_4_out, Res;

  Button button_1 (.out(Res));
  Clock #(.highDuration(1), .lowDuration(1)) clock_1 (.out(clock_1_out));
  Register #(.width(5), .trigger("rising")) register_1 (
    .D({cBlue, cGreen, cRed, cNone, nNone}), .Q({cAll, cBlue, cGreen, cRed, cNone}), .clk(clock_1_out),
    .clr(Res));  // open: en
  or or_1 (nNone, nor_1_out, cAll);
  nor nor_1 (nor_1_out, cNone, cRed, cGreen, cBlue, cAll);
  or or_2 (or_2_out, cRed, cAll);
  or or_3 (or_3_out, cGreen, cAll);
  or or_4 (or_4_out, cBlue, cAll);
  LED #(.active("true")) led_1 (.in(or_2_out));
  LED #(.active("true")) led_2 (.in(or_3_out));
  LED #(.active("true")) led_3 (.in(or_4_out));

  // Other names for the same wires on the sheet: nRed = cNone; nGreen = cRed; nBlue = cGreen; nAll = cBlue
endmodule
