// Logisim project timedlab1.circ as structural Verilog: 1 circuit, main circuit main
module main (
  input  in_1,
  input  Select_Lines,
  input  in_3,
  input  in_4,
  input  in_5,
  input  in_6,
  input  _001,
  input  _010,
  input  _011,
  input  _100,
  input  _101,
  input  _110,
  input  in_13,
  input  in_14,
  input  Most_Significant,
  input  in_16,
  input  in_17,
  input  in_18,
  input  in_19,
  input  in_20,
  input  in_21,
  input  Least_SIgnficant,
  output _000,
  output _001_2,
  output _010_2,
  output out_26,
  output _011_2,
  output _100_2,
  output _101_2,
  output _110_2,
  output _111,
  output Most_Significant_2,
  output out_33,
  output out_34,
  output out_35,
  output out_36,
  output out_37,
  output out_38,
  output out_39,
  output out_40,
  output out_41,
  output out_42,
  output out_43,
  output out_44,
  output out_45,
  output out_46,
  output out_47
);

  wire and_1_out, and_2_out, and_3_out, and_4_out, and_5_out, and_6_out, and_7_out, and_8_out, not_1_out,
       not_2_out, not_3_out, not_4_out, not_5_out, not_6_out, not_7_out, not_8_out, not_9_out, not_10_out,
       not_11_out, not_12_out, not_13_out, not_14_out, not_15_out, not_16_out, not_17_out, not_18_out,
       not_19_out, not_20_out, not_21_out, not_22_out, not_23_out, not_24_out;

  not not_1 (not_1_out, Select_Lines);
  not not_2 (not_2_out, in_1);
  not not_3 (not_3_out, in_3);
  not not_4 (not_4_out, in_1);
  not not_5 (not_5_out, in_1);
  not not_6 (not_6_out, in_3);
  not not_7 (not_7_out, Select_Lines);
  not not_8 (not_8_out, Select_Lines);
  not not_9 (not_9_out, in_3);
  not not_10 (not_10_out, in_3);
  not not_11 (not_11_out, Select_Lines);
  not not_12 (not_12_out, in_1);
  and and_1 (and_1_out, in_3, not_1_out, not_2_out, _001);
  and and_2 (and_2_out, not_3_out, Select_Lines, not_4_out, _010);
  and and_3 (and_3_out, in_3, Select_Lines, not_5_out, _011);
  and and_4 (and_4_out, not_6_out, not_7_out, in_1, _100);
  and and_5 (and_5_out, in_3, not_8_out, in_1, _101);
  and and_6 (and_6_out, not_9_out, Select_Lines, in_1, _110);
  and and_7 (and_7_out, in_3, Select_Lines, in_1, in_13);
  and and_8 (and_8_out, not_10_out, not_11_out, not_12_out, in_14);
  or or_1 (out_26, and_1_out, and_2_out, and_3_out, and_4_out, and_5_out, and_6_out, and_7_out, and_8_out);
  not not_13 (not_13_out, in_6);
  not not_14 (not_14_out, in_5);
  not not_15 (not_15_out, in_4);
  not not_16 (not_16_out, in_5);
  not not_17 (not_17_out, in_4);
  not not_18 (not_18_out, in_6);
  not not_19 (not_19_out, in_4);
  not not_20 (not_20_out, in_4);
  not not_21 (not_21_out, in_6);
  not not_22 (not_22_out, in_5);
  not not_23 (not_23_out, in_5);
  not not_24 (not_24_out, in_6);
  and and_9 (_000, not_13_out, not_14_out, not_15_out);
  and and_10 (_001_2, in_6, not_16_out, not_17_out);
  and and_11 (_010_2, not_18_out, in_5, not_19_out);
  and and_12 (_011_2, in_6, in_5, not_20_out);
  and and_13 (_100_2, not_21_out, not_22_out, in_4);
  and and_14 (_101_2, in_6, not_23_out, in_4);
  and and_15 (_110_2, not_24_out, in_5, in_4);
  and and_16 (_111, in_6, in_5, in_4);

  assign Most_Significant_2 = Most_Significant;
  assign out_33 = Most_Significant;
  assign out_34 = Most_Significant;
  assign out_35 = Most_Significant;
  assign out_36 = Most_Significant;
  assign out_37 = Most_Significant;
  assign out_38 = Most_Significant;
  assign out_39 = Most_Significant;
  assign out_40 = Most_Significant;
  assign out_41 = in_16;
  assign out_42 = in_17;
  assign out_43 = in_18;
  assign out_44 = in_19;
  assign out_45 = in_20;
  assign out_46 = in_21;
  assign out_47 = Least_SIgnficant;

  // Notes on the sheet:
  //   111
  //   000
  //   Sign Extender
  //   Multiplexer
  //   Least Significant
  //   Decoder
endmodule
