// Logisim project timedlab2.circ as structural Verilog: 1 circuit, main circuit main
module main (
  output W1,
  output W2,
  output W3,
  output W4,
  output NICE
);

  wire and_1_out, and_2_out, clock_1_out, cOFF, cW1, cW1W2NICE, cW1W2W4NICE, cW1W4, nOFF, nor_1_out,
       not_1_out, not_2_out, nW1, nW1W2, nW1W2NICE, nW1W4, ON, POLITE, RESET_out;

  Button u_ON (.out(ON));
  Button u_POLITE (.out(POLITE));
  and and_1 (and_1_out, cOFF, not_1_out);
  not not_1 (not_1_out, ON);
  and and_2 (and_2_out, cOFF, ON);
  and and_3 (nW1W2NICE, cW1, POLITE);
  and and_4 (nW1W2, cW1, not_2_out);
  not not_2 (not_2_out, POLITE);
  nor nor_1 (nor_1_out, cOFF, cW1, cW1W2NICE, cW1W2W4NICE, W2, W3, cW1W4);
  or or_1 (nOFF, nor_1_out, and_1_out);
  Register #(.width(7), .trigger("rising")) register_1 (
    .D({nW1W4, W2, nW1W2, cW1W2NICE, nW1W2NICE, nW1, nOFF}),
    .Q({cW1W4, W3, W2, cW1W2W4NICE, cW1W2NICE, cW1, cOFF}), .clk(clock_1_out), .clr(RESET_out));  // open: en
  Button RESET (.out(RESET_out));
  Clock #(.highDuration(1), .lowDuration(1)) clock_1 (.out(clock_1_out));
  or or_2 (nW1W4, cW1W2W4NICE, W3);
  or or_3 (nW1, cW1W4, and_2_out);
  or or_4 (W1, cW1, W2, cW1W2NICE, cW1W2W4NICE, W3, cW1W4);
  or or_5 (NICE, W3, cW1W2W4NICE, cW1W2NICE);
  or or_6 (W4, W3, cW1W4, cW1W2W4NICE);
  LED #(.active("true")) led_1 (.in(cOFF));

  // Other names for the same wires on the sheet: STATE[6:0] = {cW1W4, W3, W2, cW1W2W4NICE, cW1W2NICE, cW1, cOFF};
  //   nW1W2W4NICE = cW1W2NICE; cW1W2 = W2; nW1W2W3W4NICE = W2; cW1W2W3W4NICE = W3
endmodule
