// Logisim project Project1.circ as structural Verilog: 3 circuits, main circuit Datapath
module ALU (
  input  [1:0] OPCODE,
  input  [15:0] A,
  input  [15:0] B,
  output [15:0] out_4
);

  wire adder_1_cout, adder_1_out, adder_2_cout, adder_2_out, adder_3_cout, adder_3_out, adder_4_cout,
       adder_4_out, adder_5_cout, adder_5_out, adder_6_cout, adder_6_out, adder_7_cout, adder_7_out,
       adder_8_cout, adder_8_out, adder_9_cout, adder_9_out, adder_10_cout, adder_10_out, adder_11_cout,
       adder_11_out, adder_12_cout, adder_12_out, adder_13_cout, adder_13_out, adder_14_cout, adder_14_out,
       adder_15_cout, adder_15_out, adder_16_out, decoder_1_out1, decoder_1_out2, decoder_1_out3,
       multiplexer_1_out, multiplexer_2_out, multiplexer_3_out, multiplexer_4_out, multiplexer_5_out,
       multiplexer_6_out, multiplexer_7_out, multiplexer_8_out, multiplexer_9_out, multiplexer_10_out,
       multiplexer_11_out, multiplexer_12_out, multiplexer_13_out, multiplexer_14_out, multiplexer_15_out,
       nand_1_out, nand_2_out, nand_3_out, nand_4_out, nand_5_out, nand_6_out, nand_7_out, nand_8_out,
       nand_9_out, nand_10_out, nand_11_out, nand_12_out, nand_13_out, nand_14_out, nand_15_out, nand_16_out,
       not_1_out, not_2_out, not_3_out, not_4_out, not_5_out, not_6_out, not_7_out, not_8_out, not_9_out,
       not_10_out, not_11_out, not_12_out, not_13_out, not_14_out, not_15_out, not_16_out, not_17_out,
       not_18_out, not_19_out, not_20_out, not_21_out, not_22_out, not_23_out, not_24_out, not_25_out,
       not_26_out, not_27_out, not_28_out, not_29_out, not_30_out, or_1_out, xor_1_out, xor_2_out, xor_3_out,
       xor_4_out, xor_5_out, xor_6_out, xor_7_out, xor_8_out, xor_9_out, xor_10_out, xor_11_out, xor_12_out,
       xor_13_out, xor_14_out, xor_15_out, xor_16_out;

  xor xor_1 (xor_1_out, B[0], decoder_1_out2);
  xor xor_2 (xor_2_out, B[1], decoder_1_out2);
  xor xor_3 (xor_3_out, B[2], decoder_1_out2);
  xor xor_4 (xor_4_out, B[3], decoder_1_out2);
  xor xor_5 (xor_5_out, B[4], decoder_1_out2);
  xor xor_6 (xor_6_out, B[5], decoder_1_out2);
  xor xor_7 (xor_7_out, B[6], decoder_1_out2);
  xor xor_8 (xor_8_out, B[7], decoder_1_out2);
  xor xor_9 (xor_9_out, B[8], decoder_1_out2);
  xor xor_10 (xor_10_out, B[9], decoder_1_out2);
  xor xor_11 (xor_11_out, B[10], decoder_1_out2);
  xor xor_12 (xor_12_out, B[11], decoder_1_out2);
  xor xor_13 (xor_13_out, B[12], decoder_1_out2);
  xor xor_14 (xor_14_out, B[13], decoder_1_out2);
  xor xor_15 (xor_15_out, B[14], decoder_1_out2);
  xor xor_16 (xor_16_out, B[15], decoder_1_out2);
  not not_1 (not_1_out, decoder_1_out3);
  not not_2 (not_2_out, decoder_1_out3);
  not not_3 (not_3_out, decoder_1_out3);
  not not_4 (not_4_out, decoder_1_out3);
  not not_5 (not_5_out, decoder_1_out3);
  not not_6 (not_6_out, decoder_1_out3);
  not not_7 (not_7_out, decoder_1_out3);
  not not_8 (not_8_out, decoder_1_out3);
  not not_9 (not_9_out, decoder_1_out3);
  not not_10 (not_10_out, decoder_1_out3);
  not not_11 (not_11_out, decoder_1_out3);
  not not_12 (not_12_out, decoder_1_out3);
  not not_13 (not_13_out, decoder_1_out3);
  not not_14 (not_14_out, decoder_1_out3);
  not not_15 (not_15_out, decoder_1_out3);
  not not_16 (not_16_out, decoder_1_out3);
  not not_17 (not_17_out, decoder_1_out3);
  not not_18 (not_18_out, decoder_1_out3);
  not not_19 (not_19_out, decoder_1_out3);
  not not_20 (not_20_out, decoder_1_out3);
  not not_21 (not_21_out, decoder_1_out3);
  not not_22 (not_22_out, decoder_1_out3);
  not not_23 (not_23_out, decoder_1_out3);
  not not_24 (not_24_out, decoder_1_out3);
  not not_25 (not_25_out, decoder_1_out3);
  not not_26 (not_26_out, decoder_1_out3);
  not not_27 (not_27_out, decoder_1_out3);
  not not_28 (not_28_out, decoder_1_out3);
  not not_29 (not_29_out, decoder_1_out3);
  not not_30 (not_30_out, decoder_1_out3);
  Decoder #(.select(2)) decoder_1 (
    .out1(decoder_1_out1), .out2(decoder_1_out2), .out3(decoder_1_out3), .sel(OPCODE));  // open: out0, en
  or or_1 (or_1_out, xor_1_out, decoder_1_out3);
  Multiplexer multiplexer_1 (.in0(not_1_out), .in1(xor_2_out), .out(multiplexer_1_out), .sel(not_2_out));  // open: en
  Multiplexer multiplexer_2 (.in0(not_3_out), .in1(xor_3_out), .out(multiplexer_2_out), .sel(not_4_out));  // open: en
  Multiplexer multiplexer_3 (.in0(not_5_out), .in1(xor_4_out), .out(multiplexer_3_out), .sel(not_6_out));  // open: en
  Multiplexer multiplexer_4 (.in0(not_7_out), .in1(xor_5_out), .out(multiplexer_4_out), .sel(not_8_out));  // open: en
  Multiplexer multiplexer_5 (.in0(not_9_out), .in1(xor_6_out), .out(multiplexer_5_out), .sel(not_10_out));  // open: en
  Multiplexer multiplexer_6 (.in0(not_11_out), .in1(xor_7_out), .out(multiplexer_6_out), .sel(not_12_out));  // open: en
  Multiplexer multiplexer_7 (.in0(not_13_out), .in1(xor_8_out), .out(multiplexer_7_out), .sel(not_14_out));  // open: en
  Multiplexer multiplexer_8 (.in0(not_15_out), .in1(xor_9_out), .out(multiplexer_8_out), .sel(not_16_out));  // open: en
  Multiplexer multiplexer_9 (
    .in0(not_17_out), .in1(xor_10_out), .out(multiplexer_9_out), .sel(not_18_out));  // open: en
  Multiplexer multiplexer_10 (
    .in0(not_19_out), .in1(xor_11_out), .out(multiplexer_10_out), .sel(not_20_out));  // open: en
  Multiplexer multiplexer_11 (
    .in0(not_21_out), .in1(xor_12_out), .out(multiplexer_11_out), .sel(not_22_out));  // open: en
  Multiplexer multiplexer_12 (
    .in0(not_23_out), .in1(xor_13_out), .out(multiplexer_12_out), .sel(not_24_out));  // open: en
  Multiplexer multiplexer_13 (
    .in0(not_25_out), .in1(xor_14_out), .out(multiplexer_13_out), .sel(not_26_out));  // open: en
  Multiplexer multiplexer_14 (
    .in0(not_27_out), .in1(xor_15_out), .out(multiplexer_14_out), .sel(not_28_out));  // open: en
  Multiplexer multiplexer_15 (
    .in0(not_29_out), .in1(xor_16_out), .out(multiplexer_15_out), .sel(not_30_out));  // open: en
  Adder #(.width(1)) adder_1 (.a(A[0]), .b(or_1_out), .out(adder_1_out), .cin(decoder_1_out2), .cout(adder_1_cout));
  nand nand_1 (nand_1_out, A[0], or_1_out);
  Adder #(.width(1)) adder_2 (
    .a(A[1]), .b(multiplexer_1_out), .out(adder_2_out), .cin(adder_1_cout), .cout(adder_2_cout));
  nand nand_2 (nand_2_out, A[1], multiplexer_1_out);
  Adder #(.width(1)) adder_3 (
    .a(A[2]), .b(multiplexer_2_out), .out(adder_3_out), .cin(adder_2_cout), .cout(adder_3_cout));
  nand nand_3 (nand_3_out, A[2], multiplexer_2_out);
  Adder #(.width(1)) adder_4 (
    .a(A[3]), .b(multiplexer_3_out), .out(adder_4_out), .cin(adder_3_cout), .cout(adder_4_cout));
  nand nand_4 (nand_4_out, A[3], multiplexer_3_out);
  Adder #(.width(1)) adder_5 (
    .a(A[4]), .b(multiplexer_4_out), .out(adder_5_out), .cin(adder_4_cout), .cout(adder_5_cout));
  nand nand_5 (nand_5_out, A[4], multiplexer_4_out);
  Adder #(.width(1)) adder_6 (
    .a(A[5]), .b(multiplexer_5_out), .out(adder_6_out), .cin(adder_5_cout), .cout(adder_6_cout));
  nand nand_6 (nand_6_out, A[5], multiplexer_5_out);
  Adder #(.width(1)) adder_7 (
    .a(A[6]), .b(multiplexer_6_out), .out(adder_7_out), .cin(adder_6_cout), .cout(adder_7_cout));
  nand nand_7 (nand_7_out, A[6], multiplexer_6_out);
  Adder #(.width(1)) adder_8 (
    .a(A[7]), .b(multiplexer_7_out), .out(adder_8_out), .cin(adder_7_cout), .cout(adder_8_cout));
  nand nand_8 (nand_8_out, A[7], multiplexer_7_out);
  Adder #(.width(1)) adder_9 (
    .a(A[8]), .b(multiplexer_8_out), .out(adder_9_out), .cin(adder_8_cout), .cout(adder_9_cout));
  nand nand_9 (nand_9_out, A[8], multiplexer_8_out);
  Adder #(.width(1)) adder_10 (
    .a(A[9]), .b(multiplexer_9_out), .out(adder_10_out), .cin(adder_9_cout), .cout(adder_10_cout));
  nand nand_10 (nand_10_out, A[9], multiplexer_9_out);
  Adder #(.width(1)) adder_11 (
    .a(A[10]), .b(multiplexer_10_out), .out(adder_11_out), .cin(adder_10_cout), .cout(adder_11_cout));
  nand nand_11 (nand_11_out, A[10], multiplexer_10_out);
  Adder #(.width(1)) adder_12 (
    .a(A[11]), .b(multiplexer_11_out), .out(adder_12_out), .cin(adder_11_cout), .cout(adder_12_cout));
  nand nand_12 (nand_12_out, A[11], multiplexer_11_out);
  Adder #(.width(1)) adder_13 (
    .a(A[12]), .b(multiplexer_12_out), .out(adder_13_out), .cin(adder_12_cout), .cout(adder_13_cout));
  nand nand_13 (nand_13_out, A[12], multiplexer_12_out);
  Adder #(.width(1)) adder_14 (
    .a(A[13]), .b(multiplexer_13_out), .out(adder_14_out), .cin(adder_13_cout), .cout(adder_14_cout));
  nand nand_14 (nand_14_out, A[13], multiplexer_13_out);
  Adder #(.width(1)) adder_15 (
    .a(A[14]), .b(multiplexer_14_out), .out(adder_15_out), .cin(adder_14_cout), .cout(adder_15_cout));
  nand nand_15 (nand_15_out, A[14], multiplexer_14_out);
  Adder #(.width(1)) adder_16 (
    .a(A[15]), .b(multiplexer_15_out), .out(adder_16_out), .cin(adder_15_cout));  // open: cout
  nand nand_16 (nand_16_out, A[15], multiplexer_15_out);
  Multiplexer multiplexer_16 (.in0(adder_1_out), .in1(nand_1_out), .out(out_4[0]), .sel(decoder_1_out1));  // open: en
  Multiplexer multiplexer_17 (.in0(adder_2_out), .in1(nand_2_out), .out(out_4[1]), .sel(decoder_1_out1));  // open: en
  Multiplexer multiplexer_18 (.in0(adder_3_out), .in1(nand_3_out), .out(out_4[2]), .sel(decoder_1_out1));  // open: en
  Multiplexer multiplexer_19 (.in0(adder_4_out), .in1(nand_4_out), .out(out_4[3]), .sel(decoder_1_out1));  // open: en
  Multiplexer multiplexer_20 (.in0(adder_5_out), .in1(nand_5_out), .out(out_4[4]), .sel(decoder_1_out1));  // open: en
  Multiplexer multiplexer_21 (.in0(adder_6_out), .in1(nand_6_out), .out(out_4[5]), .sel(decoder_1_out1));  // open: en
  Multiplexer multiplexer_22 (.in0(adder_7_out), .in1(nand_7_out), .out(out_4[6]), .sel(decoder_1_out1));  // open: en
  Multiplexer multiplexer_23 (.in0(adder_8_out), .in1(nand_8_out), .out(out_4[7]), .sel(decoder_1_out1));  // open: en
  Multiplexer multiplexer_24 (.in0(adder_9_out), .in1(nand_9_out), .out(out_4[8]), .sel(decoder_1_out1));  // open: en
  Multiplexer multiplexer_25 (.in0(adder_10_out), .in1(nand_10_out), .out(out_4[9]), .sel(decoder_1_out1));  // open: en
  Multiplexer multiplexer_26 (
    .in0(adder_11_out), .in1(nand_11_out), .out(out_4[10]), .sel(decoder_1_out1));  // open: en
  Multiplexer multiplexer_27 (
    .in0(adder_12_out), .in1(nand_12_out), .out(out_4[11]), .sel(decoder_1_out1));  // open: en
  Multiplexer multiplexer_28 (
    .in0(adder_13_out), .in1(nand_13_out), .out(out_4[12]), .sel(decoder_1_out1));  // open: en
  Multiplexer multiplexer_29 (
    .in0(adder_14_out), .in1(nand_14_out), .out(out_4[13]), .sel(decoder_1_out1));  // open: en
  Multiplexer multiplexer_30 (
    .in0(adder_15_out), .in1(nand_15_out), .out(out_4[14]), .sel(decoder_1_out1));  // open: en
  Multiplexer multiplexer_31 (
    .in0(adder_16_out), .in1(nand_16_out), .out(out_4[15]), .sel(decoder_1_out1));  // open: en

  // Notes on the sheet:
  //   OPCODES
  //   00: C = A + B
  //   01: C = A NAND B
  //   10: C = A - B
  //   11: C = A + 1
endmodule

module Datapath (
  input  in_1
);

  wire CLOCK, comparator_1_eq, comparator_2_eq, DrALU, DrMEM, DrOFF, DrPC, DrREG, LdA, LdB, LdIR, LdMAR,
       LdPC, LdZ, multiplexer_2_out, register_1_q, WrMEM, WrREG;
  wire [1:0] bit_extender_1_out, func, REGSEL;
  wire [2:0] OP;
  wire [3:0] multiplexer_1_out, RX, RY, RZ;
  wire [4:4] IR_q;
  wire [15:0] A_q, ALU_out_4, B_q, bit_extender_2_out, controlled_buffer_1_out, MAR_q, PC_q, ram_1_data,
       ram_2_data;

  Register #(.width(16)) PC (.D(controlled_buffer_1_out), .en(LdPC), .Q(PC_q), .clk(CLOCK), .clr(in_1));
  Register #(.width(16)) B (.D(controlled_buffer_1_out), .en(LdB), .Q(B_q), .clk(CLOCK));  // open: clr
  assign controlled_buffer_1_out = DrPC ? PC_q : 16'bz;  // Controlled_Buffer controlled_buffer_1
  Comparator #(.width(16)) comparator_1 (
    .a(controlled_buffer_1_out), .b({16{1'b0}}), .eq(comparator_1_eq));  // open: gt, lt
  Clock clock_1 (.out(CLOCK));
  Register #(.width(16)) A (.D(controlled_buffer_1_out), .en(LdA), .Q(A_q), .clk(CLOCK));  // open: clr
  ALU ALU (.OPCODE(func), .A(A_q), .B(B_q), .out_4(ALU_out_4));
  assign controlled_buffer_1_out = DrALU ? ALU_out_4 : 16'bz;  // Controlled_Buffer controlled_buffer_2
  Register #(.width(1)) register_1 (.D(comparator_1_eq), .en(LdZ), .Q(register_1_q), .clk(CLOCK));  // open: clr
  Multiplexer #(.select(2), .width(4), .enable("false")) multiplexer_1 (
    .in0(RX), .in1(RY), .in2(RZ), .out(multiplexer_1_out), .sel(REGSEL));  // open: in3
  assign bit_extender_1_out = {{1{1'b0}}, register_1_q};  // Bit_Extender bit_extender_1
  Multiplexer #(.enable("false")) multiplexer_2 (
    .in0(WrREG), .in1(1'b0), .out(multiplexer_2_out), .sel(comparator_2_eq));
  Comparator #(.width(4)) comparator_2 (.a(multiplexer_1_out), .b(4'b0000), .eq(comparator_2_eq));  // open: gt, lt
  _3_ROM_Microsequencer u_3_rom_microsequencer_1 (
    .Z(bit_extender_1_out), .IR_15_13(OP), .Reset(in_1),
    .OUT({func, REGSEL, WrMEM, WrREG, LdZ, LdB, LdA, LdMAR, LdIR, LdPC, DrOFF, DrPC, DrALU, DrMEM, DrREG}),
    .CLOCK(CLOCK));
  Register #(.width(16)) MAR (.D(controlled_buffer_1_out), .en(LdMAR), .Q(MAR_q), .clk(CLOCK));  // open: clr
  RAM #(.addrWidth(4), .dataWidth(16), .bus("separate")) ram_1 (
    .addr(multiplexer_1_out), .din(controlled_buffer_1_out), .data(ram_1_data), .str(multiplexer_2_out),
    .clk(CLOCK), .ld(1'b1));  // open: sel, clr
  assign controlled_buffer_1_out = DrREG ? ram_1_data : 16'bz;  // Controlled_Buffer controlled_buffer_3
  RAM #(.addrWidth(16), .dataWidth(16), .bus("separate")) ram_2 (
    .addr(MAR_q), .din(controlled_buffer_1_out), .data(ram_2_data), .str(WrMEM), .clk(CLOCK), .ld(1'b1));  // open: sel, clr
  assign controlled_buffer_1_out = DrMEM ? ram_2_data : 16'bz;  // Controlled_Buffer controlled_buffer_4
  Register #(.width(16)) IR (
    .D(controlled_buffer_1_out), .en(LdIR), .Q({OP, RX, RY, IR_q[4], RZ}), .clk(CLOCK));  // open: clr
  assign controlled_buffer_1_out = DrOFF ? bit_extender_2_out : 16'bz;  // Controlled_Buffer controlled_buffer_5
  assign bit_extender_2_out = {{11{IR_q[4]}}, {IR_q[4], RZ}};  // Bit_Extender bit_extender_2

  // Other names for the same wires on the sheet: RES = in_1

  // Notes on the sheet:
  //   Jessie McGarry
  //   902616371
endmodule

module _3_ROM_Microsequencer (
  input  Reset,
  input  CLOCK,
  input  [1:0] Z,
  input  [2:0] IR_15_13,
  output [16:0] OUT
);

  wire [5:0] multiplexer_1_out, NextState, register_1_q, rom_2_data, rom_3_data;
  wire [24:23] rom_1_data;

  Register #(.width(6)) register_1 (.D(multiplexer_1_out), .Q(register_1_q), .clk(CLOCK), .clr(Reset));  // open: en
  ROM #(.addrWidth(6), .dataWidth(25)) rom_1 (.addr(register_1_q), .data({rom_1_data, OUT, NextState}));  // open: sel
  Multiplexer #(.select(2), .width(6), .enable("false")) multiplexer_1 (
    .in0(NextState), .in1(rom_3_data), .in2(rom_2_data), .out(multiplexer_1_out), .sel(rom_1_data));  // open: in3
  ROM #(.addrWidth(2), .dataWidth(6)) rom_2 (.addr(Z), .data(rom_2_data));  // open: sel
  ROM #(.addrWidth(3), .dataWidth(6)) rom_3 (.addr(IR_15_13), .data(rom_3_data));  // open: sel

  // Notes on the sheet:
  //   contents of rom_1 (hex, n*v repeats v):
  //   6201 1082 e00900 84044 108045 20100 84047 8408 20100 8404a 10804b 2a0100 a020d 840 8404f 8410 2111
  //   20080 84053 8414 2115 40040 4057 88058 1410100 421a 841b 900 1c
  //   contents of rom_2 (hex, n*v repeats v):
  //   0 19
  //   contents of rom_3 (hex, n*v repeats v):
  //   3 9 6 e 12 16 c 1c
endmodule
