// Logisim project LC-2200-32.circ as structural Verilog: 6 circuits, main circuit Processor
module Processor (
  input  in_1
);

  wire Clock, DrALU, DrMEM, DrOFF, DrPC, DrReg, IE, Int, Int_q, IntAck, intergenerator_1_intout, LdA, LdB,
       LdEnInt, LdIR, LdMAR, LdPC, LdZ, not_1_out, or_1_out, WrMEM, WrREG, Z, ZeroDetectOut;
  wire [1:0] FUNC, RegSel;
  wire [3:0] IR_q, IR_q_3, IR_q_4, Opcode, Reg_num;
  wire [23:0] MAR_q;
  wire [31:0] A_q, B_q, controlled_buffer_1_out, IE_q, multiplexer_1_out, PC_q, ram_1_data,
       registers_1_data_out, ZeroDetect;
  wire [31:4] IR_q_2;

  Multiplexer #(.width(32), .enable("false")) multiplexer_1 (
    .in0(controlled_buffer_1_out), .in1(32'h10), .out(multiplexer_1_out), .sel(in_1));
  Register #(.width(32)) PC (.D(multiplexer_1_out), .en(or_1_out), .Q(PC_q), .clk(Clock));  // open: clr
  or or_1 (or_1_out, in_1, LdPC);
  assign controlled_buffer_1_out = DrPC ? PC_q : 32'bz;  // Controlled_Buffer controlled_buffer_1
  Register #(.width(32)) u_IE (.D(controlled_buffer_1_out), .en(LdEnInt), .Q(IE_q), .clk(Clock));  // open: clr
  intergenerator intergenerator_1 (.IntOut(intergenerator_1_intout), .CLK(Clock));
  Register #(.width(1)) Z_Register (.D(ZeroDetectOut), .en(LdZ), .Q(Z), .clk(Clock), .clr(in_1));
  Comparator #(.width(32)) comparator_1 (.a(IE_q), .b(32'h1), .eq(IE));  // open: gt, lt
  or or_2 (Int, intergenerator_1_intout, Int_q);
  Register #(.width(1)) u_Int (
    .D(intergenerator_1_intout), .en(intergenerator_1_intout), .Q(Int_q), .clk(Clock), .clr(IntAck));
  Register #(.width(32)) A (.D(controlled_buffer_1_out), .en(LdA), .Q(A_q), .clk(Clock), .clr(in_1));
  ALU alu_1 (.FUNC(FUNC), .INPUT_A(A_q), .INPUT_B(B_q), .out_4(ZeroDetect));
  assign controlled_buffer_1_out = IntAck ? 32'h1 : 32'bz;  // Controlled_Buffer controlled_buffer_2
  Register #(.width(32)) B (.D(controlled_buffer_1_out), .en(LdB), .Q(B_q), .clk(Clock), .clr(in_1));
  assign controlled_buffer_1_out = DrALU ? ZeroDetect : 32'bz;  // Controlled_Buffer controlled_buffer_3
  State_Machine state_machine_1 (
    .Clock(Clock), .OpCode(Opcode), .Z(Z), .IE(IE), .Int(Int), .DrREG(DrReg), .DrMEM(DrMEM), .DrALU(DrALU),
    .DrPC(DrPC), .DrOFF(DrOFF), .LdPC(LdPC), .LdIR(LdIR), .LdMAR(LdMAR), .LdA(LdA), .LdB(LdB), .LdZ(LdZ),
    .WrREG(WrREG), .WrMEM(WrMEM), .RegSel(RegSel), .ALU_FUNC(FUNC), .LdEnInt(LdEnInt), .IntAck(IntAck));
  Registers registers_1 (
    .WrReg(WrREG), .RegSel(Reg_num), .Data_In(controlled_buffer_1_out), .Clock(Clock), .ClearRegFile(in_1),
    .Data_Out(registers_1_data_out));
  assign controlled_buffer_1_out = DrReg ? registers_1_data_out : 32'bz;  // Controlled_Buffer controlled_buffer_4
  Clock clock_1 (.out(Clock));
  Register #(.width(24)) MAR (.D(controlled_buffer_1_out[23:0]), .en(LdMAR), .Q(MAR_q), .clk(Clock), .clr(in_1));
  not not_1 (not_1_out, WrMEM);
  RAM #(.addrWidth(24), .dataWidth(32), .bus("separate")) ram_1 (
    .addr(MAR_q), .din(controlled_buffer_1_out), .data(ram_1_data), .str(WrMEM), .clk(Clock), .ld(not_1_out),
    .clr(in_1));  // open: sel
  assign controlled_buffer_1_out = DrMEM ? ram_1_data : 32'bz;  // Controlled_Buffer controlled_buffer_5
  Register #(.width(32)) IR (
    .D(controlled_buffer_1_out), .en(LdIR), .Q({Opcode, IR_q_4, IR_q_3, IR_q_2[31], IR_q_2[18:4], IR_q}),
    .clk(Clock), .clr(in_1));
  Multiplexer #(.select(2), .width(4), .enable("false")) multiplexer_2 (
    .in0(IR_q_4), .in1(IR_q_3), .in2(IR_q), .in3(4'b1100), .out(Reg_num), .sel(RegSel));
  assign controlled_buffer_1_out = DrOFF ? {{13{IR_q_2[31]}}, IR_q_2[18:4], IR_q} : 32'bz;  // Controlled_Buffer controlled_buffer_6
  Comparator #(.width(32), .mode("unsigned")) comparator_2 (
    .a(ZeroDetect), .b({32{1'b0}}), .eq(ZeroDetectOut));  // open: gt, lt

  // Other names for the same wires on the sheet: Clr = in_1

  // Notes on the sheet:
  //   00 = RX
  //   01 = RY
  //   10 = RZ
endmodule

module ALU (
  input  [31:0] INPUT_A,
  input  [31:0] INPUT_B,
  input  [1:0] FUNC,
  output [31:0] out_4
);

  wire [31:0] adder_1_out, adder_2_out, nand_1_out, subtractor_1_out;

  Adder #(.width(32)) adder_1 (.a(INPUT_A), .b(INPUT_B), .out(adder_1_out));  // open: cin, cout
  assign nand_1_out = ~(INPUT_A & INPUT_B);  // NAND_Gate nand_1, 32 bits wide
  Multiplexer #(.select(2), .width(32), .enable("false")) multiplexer_1 (
    .in0(adder_1_out), .in1(nand_1_out), .in2(subtractor_1_out), .in3(adder_2_out), .out(out_4), .sel(FUNC));
  Subtractor #(.width(32)) subtractor_1 (.a(INPUT_A), .b(INPUT_B), .out(subtractor_1_out));  // open: bin, bout
  Adder #(.width(32)) adder_2 (.a(INPUT_A), .b(32'h1), .out(adder_2_out));  // open: cin, cout
endmodule

module State_Machine (
  input  Clock,
  input  [3:0] OpCode,
  input  Z,
  input  IE,
  input  Int,
  output DrREG,
  output DrMEM,
  output DrALU,
  output DrPC,
  output DrOFF,
  output LdPC,
  output LdIR,
  output LdMAR,
  output LdA,
  output LdB,
  output LdZ,
  output WrREG,
  output WrMEM,
  output [1:0] RegSel,
  output [1:0] ALU_FUNC,
  output LdEnInt,
  output IntAck
);

  wire chkZ, OpTest;
  wire [0:0] and_1_out;
  wire [5:0] multiplexer_1_out, register_1_q, rom_1_data, rom_2_data, rom_3_data, rom_4_data;
  wire [26:26] rom_2_data_2;

  and and_1 (and_1_out[0], IE, Int);
  Register #(.width(6)) register_1 (.D(multiplexer_1_out), .en(Clock), .Q(register_1_q), .clk(Clock));  // open: clr
  Multiplexer #(.select(2), .width(6), .enable("false")) multiplexer_1 (
    .in0(rom_2_data), .in1(rom_3_data), .in2(rom_4_data), .in3(rom_1_data), .out(multiplexer_1_out),
    .sel({chkZ, OpTest}));
  ROM #(.addrWidth(2), .dataWidth(6)) rom_1 (.addr({1'b0, and_1_out[0]}), .data(rom_1_data));  // open: sel
  ROM #(.addrWidth(6), .dataWidth(28)) rom_2 (
    .addr(register_1_q),
    .data({IntAck, rom_2_data_2[26], LdEnInt, chkZ, OpTest, ALU_FUNC, RegSel, WrMEM, WrREG, LdZ, LdB, LdA, LdMAR, LdIR, LdPC, DrOFF, DrPC, DrALU, DrMEM, DrREG, rom_2_data}));  // open: sel
  ROM #(.addrWidth(4), .dataWidth(6)) rom_3 (.addr(OpCode), .data(rom_3_data));  // open: sel
  ROM #(.addrWidth(2), .dataWidth(6)) rom_4 (.addr({1'b0, Z}), .data(rom_4_data));  // open: sel

  // Notes on the sheet:
  //   contents of rom_1 (hex, n*v repeats v):
  //   1 4
  //   contents of rom_2 (hex, n*v repeats v):
  //   1800000 6202 1083 e00900 1a0205 2000406 8002007 881 4049 8804a 120100 404c 840d a0100 404f 88050
  //   320100 a0212 840 4054 8415 2116 a0080 4058 8419 211a c0040 405c 8805d 41011e 1000000 4220 8421 900
  //   22 4424 2600100 2000400 180863 4*0 227
  //   contents of rom_3 (hex, n*v repeats v):
  //   8 e b 13 17 1b 11 22 29 2a 23 25 26 27 28
  //   contents of rom_4 (hex, n*v repeats v):
  //   0 1f
endmodule

// 0?
module Zero_Detection (
  input  [31:0] In,
  output Out
);

  Comparator #(.width(32), .mode("unsigned")) comparator_1 (.a(In), .b({32{1'b0}}), .eq(Out));  // open: gt, lt
endmodule

// Reg File
module Registers (
  input  [31:0] Data_In,
  input  WrReg,
  input  [3:0] RegSel,
  input  Clock,
  input  ClearRegFile,
  output [31:0] Data_Out
);

  wire and_1_out, and_2_out, and_3_out, and_4_out, and_5_out, and_6_out, and_7_out, and_8_out, and_9_out,
       and_10_out, and_11_out, and_12_out, and_13_out, and_14_out, and_15_out, and_16_out, decoder_1_out0,
       decoder_1_out1, decoder_1_out2, decoder_1_out3, decoder_1_out4, decoder_1_out5, decoder_1_out6,
       decoder_1_out7, decoder_1_out8, decoder_1_out9, decoder_1_out10, decoder_1_out11, decoder_1_out12,
       decoder_1_out13, decoder_1_out14, decoder_1_out15;
  wire [31:0] a0, a1, a2, at, k0, pr, ra, s0, s1, s2, sp, t0, t1, t2, v0, zero;

  Decoder #(.select(4), .enable("false")) decoder_1 (
    .out0(decoder_1_out0), .out1(decoder_1_out1), .out2(decoder_1_out2), .out3(decoder_1_out3),
    .out4(decoder_1_out4), .out5(decoder_1_out5), .out6(decoder_1_out6), .out7(decoder_1_out7),
    .out8(decoder_1_out8), .out9(decoder_1_out9), .out10(decoder_1_out10), .out11(decoder_1_out11),
    .out12(decoder_1_out12), .out13(decoder_1_out13), .out14(decoder_1_out14), .out15(decoder_1_out15),
    .sel(RegSel));
  and and_1 (and_1_out, decoder_1_out0, WrReg);
  and and_2 (and_2_out, decoder_1_out1, WrReg);
  and and_3 (and_3_out, decoder_1_out2, WrReg);
  and and_4 (and_4_out, decoder_1_out3, WrReg);
  and and_5 (and_5_out, decoder_1_out4, WrReg);
  and and_6 (and_6_out, decoder_1_out5, WrReg);
  and and_7 (and_7_out, decoder_1_out6, WrReg);
  and and_8 (and_8_out, decoder_1_out7, WrReg);
  and and_9 (and_9_out, decoder_1_out8, WrReg);
  and and_10 (and_10_out, decoder_1_out9, WrReg);
  and and_11 (and_11_out, decoder_1_out10, WrReg);
  and and_12 (and_12_out, decoder_1_out11, WrReg);
  and and_13 (and_13_out, decoder_1_out12, WrReg);
  and and_14 (and_14_out, decoder_1_out13, WrReg);
  and and_15 (and_15_out, decoder_1_out14, WrReg);
  and and_16 (and_16_out, decoder_1_out15, WrReg);
  Register #(.width(32)) u_zero (.D(Data_In), .en(and_1_out), .Q(zero), .clk(Clock), .clr(1'b1));
  Register #(.width(32)) u_at (.D(Data_In), .en(and_2_out), .Q(at), .clk(Clock), .clr(ClearRegFile));
  Register #(.width(32)) u_v0 (.D(Data_In), .en(and_3_out), .Q(v0), .clk(Clock), .clr(ClearRegFile));
  Register #(.width(32)) u_a0 (.D(Data_In), .en(and_4_out), .Q(a0), .clk(Clock), .clr(ClearRegFile));
  Register #(.width(32)) u_a1 (.D(Data_In), .en(and_5_out), .Q(a1), .clk(Clock), .clr(ClearRegFile));
  Register #(.width(32)) u_a2 (.D(Data_In), .en(and_6_out), .Q(a2), .clk(Clock), .clr(ClearRegFile));
  Register #(.width(32)) u_t0 (.D(Data_In), .en(and_7_out), .Q(t0), .clk(Clock), .clr(ClearRegFile));
  Register #(.width(32)) u_t1 (.D(Data_In), .en(and_8_out), .Q(t1), .clk(Clock), .clr(ClearRegFile));
  Register #(.width(32)) u_t2 (.D(Data_In), .en(and_9_out), .Q(t2), .clk(Clock), .clr(ClearRegFile));
  Register #(.width(32)) u_s0 (.D(Data_In), .en(and_10_out), .Q(s0), .clk(Clock), .clr(ClearRegFile));
  Register #(.width(32)) u_s1 (.D(Data_In), .en(and_11_out), .Q(s1), .clk(Clock), .clr(ClearRegFile));
  Register #(.width(32)) u_s2 (.D(Data_In), .en(and_12_out), .Q(s2), .clk(Clock), .clr(ClearRegFile));
  Register #(.width(32)) u_k0 (.D(Data_In), .en(and_13_out), .Q(k0), .clk(Clock), .clr(ClearRegFile));
  Register #(.width(32)) u_sp (.D(Data_In), .en(and_14_out), .Q(sp), .clk(Clock), .clr(ClearRegFile));
  Register #(.width(32)) u_pr (.D(Data_In), .en(and_15_out), .Q(pr), .clk(Clock), .clr(ClearRegFile));
  Register #(.width(32)) u_ra (.D(Data_In), .en(and_16_out), .Q(ra), .clk(Clock), .clr(ClearRegFile));
  Multiplexer #(.select(4), .width(32), .enable("false")) multiplexer_1 (
    .in0(zero), .in1(at), .in2(v0), .in3(a0), .in4(a1), .in5(a2), .in6(t0), .in7(t1), .in8(t2), .in9(s0),
    .in10(s1), .in11(s2), .in12(k0), .in13(sp), .in14(pr), .in15(ra), .out(Data_Out), .sel(RegSel));

  // Other names for the same wires on the sheet: Din[31:0] = Data_In; en = WrReg
endmodule

module intergenerator (
  input  CLK,
  output IntOut
);

  wire [9:0] adder_1_out, register_1_q;

  Adder #(.width(10)) adder_1 (.a(10'h1), .b(register_1_q), .out(adder_1_out));  // open: cin, cout
  Register #(.width(10)) register_1 (.D(adder_1_out), .en(1'b1), .Q(register_1_q), .clk(CLK));  // open: clr
  Comparator #(.width(10), .mode("unsigned")) comparator_1 (
    .a({10{1'b1}}), .b(register_1_q), .eq(IntOut));  // open: gt, lt
endmodule
