// Logisim project intergenerator.circ as structural Verilog: 1 circuit, main circuit main
module main (
  input  CLK,
  output IntOut
);

  wire [9:0] adder_1_out, register_1_q;

  Adder #(.width(10)) adder_1 (.a(10'h1), .b(register_1_q), .out(adder_1_out));  // open: cin, cout
  Register #(.width(10), .trigger("rising")) register_1 (
    .D(adder_1_out), .en(1'b1), .Q(register_1_q), .clk(CLK));  // open: clr
  Comparator #(.width(10), .mode("unsigned")) comparator_1 (
    .a({10{1'b1}}), .b(register_1_q), .eq(IntOut));  // open: gt, lt
endmodule
